// Logisim project Project2.circ as structural Verilog: 6 circuits, main circuit MIPS32
module MIPS32 (
  input  in_1,
  input  in_2
);

  wire clock_1_out, ctrlidex_1_itype, registerfile_1_p4, registerfile_1_p6, registerfile_1_p7;
  wire [3:0] ctrlidex_1_alu;
  wire [31:0] bit_extender_1_out, CTRL_q, ctrlidex_1_ctrl, D_q, idex_1_qa, idex_1_qb, idex_1_qimm,
       incrementer4_1_out_2, mips_alu_1_p4, mipsprogramrom_1_p2, multiplexer_1_out, multiplexer_2_out,
       pc_1_o, register_1_q, registerfile_1_p2, registerfile_1_p5, registerfile_1_p10, registerfile_1_p11;

  PC pc_1 (.I(incrementer4_1_out_2), .Reset(in_1), .C(clock_1_out), .Reset2(in_2), .O(pc_1_o));
  Incrementer4 incrementer4_1 (.in_1(pc_1_o), .out_2(incrementer4_1_out_2));
  // Probe on incrementer4_1_out_2
  // MIPSProgramROM mipsprogramrom_1: pin names not known; wires that end beside it: pc_1_o, mipsprogramrom_1_p2
  Register #(.width(32)) register_1 (.D(mipsprogramrom_1_p2), .clk(clock_1_out), .Q(register_1_q));  // open: en, clr
  Clock clock_1 (.out(clock_1_out));
  // RegisterFile registerfile_1: pin names not known; wires that end beside it: register_1_q, registerfile_1_p2, clock_1_out, registerfile_1_p4, registerfile_1_p5, registerfile_1_p6, registerfile_1_p7, registerfile_1_p6, registerfile_1_p7, registerfile_1_p10, registerfile_1_p11
  assign bit_extender_1_out = {{16{register_1_q[15]}}, register_1_q[15:0]};  // Bit_Extender bit_extender_1
  IDEX idex_1 (
    .C(clock_1_out), .DA(registerfile_1_p10), .DB(registerfile_1_p11), .DIMM(bit_extender_1_out),
    .QA(idex_1_qa), .QB(idex_1_qb), .QIMM(idex_1_qimm));
  CtrlIDEX ctrlidex_1 (
    .D(registerfile_1_p5), .C(clock_1_out), .IType(ctrlidex_1_itype), .Ctrl(ctrlidex_1_ctrl),
    .ALU(ctrlidex_1_alu));
  Multiplexer #(.width(32), .enable("false")) multiplexer_1 (
    .in0(mips_alu_1_p4), .in1(idex_1_qa), .out(multiplexer_1_out));  // open: sel
  Multiplexer #(.width(32), .enable("false")) multiplexer_2 (
    .in0(idex_1_qb), .in1(idex_1_qimm), .out(multiplexer_2_out), .sel(ctrlidex_1_itype));
  // Mips_ALU mips_alu_1: pin names not known; wires that end beside it: multiplexer_1_out, multiplexer_2_out, ctrlidex_1_alu, mips_alu_1_p4
  Register #(.width(32)) D (.D(mips_alu_1_p4), .clk(clock_1_out), .Q(D_q));  // open: en, clr
  Register #(.width(32)) CTRL (.D(ctrlidex_1_ctrl), .clk(clock_1_out), .Q(CTRL_q));  // open: en, clr
  Register #(.width(32)) D_2 (.D(D_q), .clk(clock_1_out), .Q(registerfile_1_p2));  // open: en, clr
  Register #(.width(32)) CTRL_2 (.D(CTRL_q), .clk(clock_1_out));  // open: en, Q, clr

  // Notes on the sheet:
  //   Data?
  //   Write Enabled
  //   Decode
  //   SELECTORS
endmodule

module Incrementer4 (
  input  [31:0] in_1,
  output [31:0] out_2
);

  wire bit_extender_1_out, incrementer_1_p2, not_1_out;
  wire [1:1] and_1_out;
  wire [29:0] bit_extender_2_out;

  Bit_Extender #(.in_width(32), .out_width(1), .\type ("zero")) bit_extender_1 (.in(in_1), .out(bit_extender_1_out));
  and and_1 (and_1_out[1], bit_extender_1_out, not_1_out);
  not not_1 (not_1_out, bit_extender_1_out);
  // Incrementer #(.width(1)) incrementer_1: pin names not known; wires that end beside it: and_1_out[1], incrementer_1_p2
  assign bit_extender_2_out = {{29{1'b0}}, incrementer_1_p2};  // Bit_Extender bit_extender_2
  assign out_2 = {bit_extender_2_out, {2{and_1_out[1]}}} ^ in_1;  // XOR_Gate xor_1, 32 bits wide
endmodule

module PC (
  input  [31:0] I,
  input  Reset,
  input  C,
  input  Reset2,
  output [31:0] O
);

  wire not_1_out, or_1_out;
  wire [31:0] multiplexer_1_out;

  Multiplexer #(.width(32), .enable("false")) multiplexer_1 (
    .in0({32{1'b0}}), .in1(I), .out(multiplexer_1_out), .sel(not_1_out));
  not not_1 (not_1_out, Reset);
  or or_1 (or_1_out, C, Reset2);
  Register #(.width(32)) register_1 (.D(multiplexer_1_out), .clk(or_1_out), .Q(O));  // open: en, clr
endmodule

module IDEX (
  input  C,
  input  [31:0] DA,
  input  [31:0] DB,
  input  [31:0] DIMM,
  output [31:0] QA,
  output [31:0] QB,
  output [31:0] QIMM
);

  Register #(.width(32)) register_1 (.D(DA), .clk(C), .Q(QA));  // open: en, clr
  Register #(.width(32)) register_2 (.D(DB), .clk(C), .Q(QB));  // open: en, clr
  Register #(.width(32)) register_3 (.D(DIMM), .clk(C), .Q(QIMM));  // open: en, clr
endmodule

module CtrlIDEX (
  input  [31:0] D,
  input  C,
  output IType,
  output [31:0] Ctrl,
  output [3:0] ALU
);

  wire not_1_out;

  Register #(.width(32)) register_1 (.D(D), .clk(C), .Q({Ctrl[31:3], ALU[3:2], Ctrl[0]}));  // open: en, clr
  and and_1 (IType, ~Ctrl[31], ~Ctrl[30], Ctrl[29]);  // AND_Gate
  and and_2 (ALU[1], Ctrl[5], Ctrl[0]);
  not not_1 (not_1_out, Ctrl[5]);
  and and_3 (ALU[0], not_1_out, Ctrl[0]);

  assign Ctrl[2:1] = ALU[3:2];
endmodule

module test (
  input  I5,
  input  I4,
  input  I3,
  input  I2,
  input  I1,
  input  I0,
  output O3,
  output O2,
  output O1,
  output O0
);

  wire not_1_out;

  and and_1 (O1, I5, I0);
  not not_1 (not_1_out, I5);
  and and_2 (O0, not_1_out, I0);

  assign O2 = I1;
  assign O3 = I2;
endmodule
